// Logisim project 16-bit ALU.circ as structural Verilog
// 1- bit
module _1_bit_ALU (
  input  A,
  input  B,
  input  [2:0] Operation,
  input  Cin,
  input  Sub,
  input  Less,
  output Result,
  output Cout,
  output Set
);

  wire AND_out, NOR_out, OR_out, xor_1_out, XOR_2_out;

  xor xor_1 (xor_1_out, B, Sub);
  and AND (AND_out, A, B);
  or OR (OR_out, A, B);
  xor XOR_2 (XOR_2_out, A, B);
  nor NOR (NOR_out, A, B);
  Adder #(.width(1)) adder_1 (.a(A), .b(xor_1_out), .out(Set), .cin(Cin), .cout(Cout));
  Multiplexer #(.select(3)) multiplexer_1 (
    .in0(AND_out), .in1(OR_out), .in2(XOR_2_out), .in3(NOR_out), .in4(Set), .in5(Less), .out(Result),
    .sel(Operation));  // open: in6, in7, en
endmodule

module _16_bits_ALU (
  input  [15:0] A,
  input  [15:0] B,
  input  Sub,
  input  [2:0] Operation,
  output [15:0] result,
  output Zero_flag,
  output Overflow,
  output Cout
);

  wire n1_bit_alu_4_p11, n1_bit_alu_7_p10, n1_bit_alu_7_p12, n1_bit_alu_9_p16, n1_bit_alu_10_p16,
       n1_bit_alu_11_p15, n1_bit_alu_11_p17, n1_bit_alu_13_p19, n1_bit_alu_14_p16, n1_bit_alu_15_p19;

  // _1_bit_ALU 1_bit_alu_1: pin names not known; wires that end beside it: {Operation[2:1], A[7]}, {Operation[2:1], A[7]}, A[0], B[0], A[1], B[1], 1'b0
  // _1_bit_ALU 1_bit_alu_2: pin names not known; wires that end beside it: {Operation[2:1], A[7]}, {Operation[2:1], A[7]}, {Operation[2:1], A[7]}, {Operation[2:1], A[7]}, {Operation[2:1], A[7]}, {Operation[2:1], A[7]}, B[0], A[1], 1'b0, B[2], 1'b0
  // _1_bit_ALU 1_bit_alu_3: pin names not known; wires that end beside it: {Operation[2:1], A[7]}, {Operation[2:1], A[7]}, {Operation[2:1], A[7]}, {Operation[2:1], A[7]}, {Operation[2:1], A[7]}, {Operation[2:1], A[7]}, 1'b0, 1'b0, A[3], B[3], 1'b0
  // _1_bit_ALU 1_bit_alu_4: pin names not known; wires that end beside it: {Operation[2:1], A[7]}, {Operation[2:1], A[7]}, {Operation[2:1], A[7]}, {Operation[2:1], A[7]}, 1'b0, A[3], B[3], 1'b0, B[4], 1'b0, n1_bit_alu_4_p11
  // _1_bit_ALU 1_bit_alu_5: pin names not known; wires that end beside it: {Operation[2:1], A[7]}, {Operation[2:1], A[7]}, {Operation[2:1], A[7]}, {Operation[2:1], A[7]}, A[3], B[3], 1'b0, B[4], 1'b0, A[5], B[5], 1'b0, n1_bit_alu_4_p11, n1_bit_alu_4_p11
  // _1_bit_ALU 1_bit_alu_6: pin names not known; wires that end beside it: {Operation[2:1], A[7]}, {Operation[2:1], A[7]}, {Operation[2:1], A[7]}, {Operation[2:1], A[7]}, {Operation[2:1], A[7]}, {Operation[2:1], A[7]}, B[4], 1'b0, A[5], 1'b0, A[6], B[6], 1'b0, n1_bit_alu_4_p11, n1_bit_alu_4_p11
  // _1_bit_ALU 1_bit_alu_7: pin names not known; wires that end beside it: {Operation[2:1], A[7]}, {Operation[2:1], A[7]}, {Operation[2:1], A[7]}, {Operation[2:1], A[7]}, 1'b0, A[6], 1'b0, B[7], 1'b0, n1_bit_alu_7_p10, n1_bit_alu_7_p10, n1_bit_alu_7_p12
  _1_bit_ALU u_1_bit_alu_8 (.A(A[7]), .B(A[7]), .Sub(A[7]), .Less(A[7]));  // open: Result, Cin, Cout, Operation, Set
  // _1_bit_ALU 1_bit_alu_9: pin names not known; wires that end beside it: {Operation[2:1], A[7]}, {Operation[2:1], A[7]}, {Operation[2:1], A[7]}, {Operation[2:1], A[7]}, {Operation[2:1], A[7]}, result[0], result[1], A[8], B[8], 1'b0, A[9], B[9], 1'b0, {Operation[2:1], A[7]}, n1_bit_alu_7_p12, n1_bit_alu_9_p16, n1_bit_alu_9_p16, {Operation[2:1], A[7]}
  // _1_bit_ALU 1_bit_alu_10: pin names not known; wires that end beside it: {Operation[2:1], A[7]}, {Operation[2:1], A[7]}, result[0], result[1], result[2], {Operation[2:1], A[7]}, B[8], 1'b0, A[9], 1'b0, A[10], B[10], 1'b0, n1_bit_alu_9_p16, n1_bit_alu_9_p16, n1_bit_alu_10_p16, n1_bit_alu_10_p16
  // _1_bit_ALU 1_bit_alu_11: pin names not known; wires that end beside it: {Operation[2:1], A[7]}, {Operation[2:1], A[7]}, result[1], result[2], result[3], {Operation[2:1], A[7]}, A[11], 1'b0, A[10], 1'b0, B[11], 1'b0, n1_bit_alu_10_p16, n1_bit_alu_10_p16, n1_bit_alu_11_p15, n1_bit_alu_11_p15, n1_bit_alu_11_p17
  // _1_bit_ALU 1_bit_alu_12: pin names not known; wires that end beside it: n1_bit_alu_4_p11, {Operation[2:1], A[7]}, {Operation[2:1], A[7]}, result[2], result[3], result[4], {Operation[2:1], A[7]}, A[10], 1'b0, A[11], B[11], 1'b0, A[12], B[12], 1'b0, n1_bit_alu_11_p15, n1_bit_alu_11_p15, n1_bit_alu_11_p17, n1_bit_alu_11_p17
  // _1_bit_ALU 1_bit_alu_13: pin names not known; wires that end beside it: n1_bit_alu_4_p11, n1_bit_alu_4_p11, {Operation[2:1], A[7]}, {Operation[2:1], A[7]}, result[3], result[4], result[5], {Operation[2:1], A[7]}, {Operation[2:1], A[7]}, B[11], 1'b0, A[12], 1'b0, A[13], B[13], 1'b0, n1_bit_alu_11_p17, n1_bit_alu_11_p17, n1_bit_alu_13_p19, n1_bit_alu_13_p19
  // _1_bit_ALU 1_bit_alu_14: pin names not known; wires that end beside it: n1_bit_alu_4_p11, n1_bit_alu_4_p11, n1_bit_alu_7_p10, result[5], result[6], result[4], {Operation[2:1], A[7]}, 1'b0, A[13], 1'b0, A[14], B[14], 1'b0, n1_bit_alu_13_p19, n1_bit_alu_13_p19, n1_bit_alu_14_p16, n1_bit_alu_14_p16
  // _1_bit_ALU 1_bit_alu_15: pin names not known; wires that end beside it: n1_bit_alu_7_p10, n1_bit_alu_7_p10, n1_bit_alu_7_p12, {Operation[2:1], A[7]}, {Operation[2:1], A[7]}, result[5], result[6], result[7], {Operation[2:1], A[7]}, {Operation[2:1], A[7]}, 1'b0, A[14], 1'b0, A[15], B[15], 1'b0, n1_bit_alu_14_p16, n1_bit_alu_14_p16, n1_bit_alu_15_p19, n1_bit_alu_15_p19
  // _1_bit_ALU 1_bit_alu_16: pin names not known; wires that end beside it: n1_bit_alu_7_p10, n1_bit_alu_7_p10, n1_bit_alu_7_p12, {Operation[2:1], A[7]}, {Operation[2:1], A[7]}, result[7], result[6], 1'b0, A[15], 1'b0, {Operation[2:1], A[7]}, {Operation[2:1], A[7]}, n1_bit_alu_15_p19, n1_bit_alu_15_p19, Cout, {Operation[2:1], A[7]}, {Operation[2:1], A[7]}, {Operation[2:1], A[7]}
  xor xor_1 (Overflow, n1_bit_alu_15_p19, Cout);
  nor nor_1 (Zero_flag, result[0], result[1], result[2], result[3], result[4], result[5], result[6], result[7], result[8], result[9], result[10], result[11], result[12], result[13], result[14], result[15]);
  // Pins of 1 and 3 bits meet at {Operation[2:1], A[7]}

  assign {A[4], A[2]} = {2{A[7]}};
  assign Operation[0] = A[7];
  assign Sub = A[7];

  // Other names for the same wires on the sheet: A2[2:0] = {Operation[2:1], A[7]}; A4[2:0] = {Operation[2:1], A[7]};
  //   A7[2:0] = {Operation[2:1], A[7]}
endmodule

module _16_bit_b (
  input  [15:0] A,
  input  [15:0] B,
  input  [2:0] Operation,
  input  Cin,
  input  Cin_2,
  output [15:0] Result,
  output Result_2,
  output Cout,
  output Cout_2
);

  wire comparator_1_gt, comparator_1_lt;
  wire [15:0] adder_1_out, AND_out, bit_extender_1_out, NOR_out, OR_out, subtractor_1_out, XOR_out;

  assign AND_out = A & B;  // AND_Gate AND, 16 bits wide
  assign OR_out = A | B;  // OR_Gate OR, 16 bits wide
  assign XOR_out = A ^ B;  // XOR_Gate XOR, 16 bits wide
  assign NOR_out = ~(A | B);  // NOR_Gate NOR, 16 bits wide
  Adder #(.width(16)) adder_1 (.a(A), .b(B), .out(adder_1_out), .cin(Cin), .cout(Cout));
  Subtractor #(.width(16)) subtractor_1 (.a(A), .b(B), .out(subtractor_1_out), .bin(Cin_2), .bout(Cout_2));
  Comparator #(.width(16)) comparator_1 (
    .a(A), .b(B), .gt(comparator_1_gt), .eq(comparator_1_gt), .lt(comparator_1_lt));
  assign bit_extender_1_out = {{15{1'b0}}, comparator_1_lt};  // Bit_Extender bit_extender_1
  Multiplexer #(.select(3), .width(16)) multiplexer_1 (
    .in0(AND_out), .in1(OR_out), .in2(XOR_out), .in3(NOR_out), .in4(adder_1_out), .in5(subtractor_1_out),
    .in6(bit_extender_1_out), .out(Result), .sel(Operation));  // open: in7, en
  nor nor_2 (Result_2, Result[0], Result[1], Result[2], Result[3], Result[4], Result[5], Result[6], Result[7], Result[8], Result[9], Result[10], Result[11], Result[12], Result[13], Result[14], Result[15]);
endmodule
